# Fritzing sketch MIDI_IN (saved by Fritzing 0.9.3b)
breadboards: 1

parts:
  U1 = MIDI_CONN_FEMALE [package=din_5_female]
  U2 = MIDI_CONN_FEMALE [package=din_5_female]  # not connected
  U3 = OPTO_DARL_6N138S [package=8-smd]  # not connected
  D1 = Diode [package=diode-1n4001]
  R1 = Resistor [tolerance=±5% resistance=220 package="0805 [SMD]"]
  R2 = Resistor [tolerance=±5% resistance=10k package="0805 [SMD]"]
  R3 = Resistor [tolerance=±5% resistance=470 package="0805 [SMD]"]
  Part1 = Arduino Nano (Rev3.0)

nets:
  N1: U1.NC1, R2.Pin_1, Part1.GND
  N2: U1.MIDI_OUT, R1.Pin_0
  N3: D1.C, R1.Pin_1
  N4: R3.Pin_0, Part1.3V3
