# Fritzing sketch MIDI_OUT (saved by Fritzing 0.9.3b)
breadboards: 2

parts:
  R1 = Slide Potentiometer [maximum_resistance=100kΩ]
  S1 = Pushbutton [package="[THT]"]
  U1 = POT [package=alps_pot]
  Part1 = Arduino Nano (Rev3.0)
  R2 = Resistor [tolerance=±5% resistance=10k package="2512 [SMD]"]
  U2 = MIDI_CONN_FEMALE [package=din_5_female]
  R3 = Resistor [tolerance=±5% resistance=220 package="2512 [SMD]"]

nets:
  N1: R1.leg1, U1.E, Part1.GND, R2.Pin_0
  N2: R1.wiper, Part1.A1
  N3: R1.leg2, S1.Pin_1, S1.Pin_2, U1.A, Part1.3V3
  N4: S1.Pin_3, S1.Pin_4, Part1.D2, R2.Pin_1
  N5: U1.S, Part1.A0
  N6: Part1.D1/TX, U2.MIDI_IN
  N7: U2.MIDI_OUT, R3.Pin_1

notes:
  Potentiometer
  Momentary Switch
  Sliding Potentiometer
  MIDI OUT
