# Fritzing sketch MIDI_TESTING (saved by Fritzing 0.9.3b)
perfboards: 1

parts:
  U1 = MIDI_CONN_FEMALE [package=din_5_female]
  U2 = MIDI_CONN_FEMALE [package=din_5_female]
  U3 = IC, DIP package, 8 pins [chip_label=6N178]
  R1 = Resistor [tolerance=±5% resistance=220 package="0805 [SMD]"]
  D1 = Diode [package=diode-1n4148]
  R2 = Resistor [tolerance=±5% resistance=470 package="0805 [SMD]"]
  R3 = Resistor [tolerance=±5% resistance=10k package="0805 [SMD]"]
  LED1 = LED - 3mm [color="Red (633nm)" package="3 mm [THT]"]
  R4 = Resistor [tolerance=±5% resistance=220 package="0805 [SMD]"]
  R5 = Resistor [tolerance=±5% resistance=220 package="0805 [SMD]"]  # not connected
  J1 = female pin header, 5 pins [form="♀ (female)"]

nets:
  N1: U1.NC1, U2.NC1
  N2: U1.MIDI_IN, J1.pin5
  N3: U2.MIDI_IN, U3.pin3
  N4: U3.pin5, R3.Pin_1
  N5: U3.pin6, J1.pin1
  N6: U3.pin8, R2.Pin_0
  N7: R1.Pin_1, D1.C
  N8: LED1.anode, R4.Pin_0

notes:
  YELLOW = RX
  BLUE = DIGI PIN
  RED = 3.3v or 5v
  BLACK = GROUND
  CYAN = TX
